// Logisim project JK_master_slave.circ as structural Verilog: 1 circuit, main circuit main
module main (
  input  j,
  input  k,
  output Q,
  output Q_prime,
  output Q_2,
  output Q_prime_2
);

  wire clock_1_out, j_k_ff_1_q, j_k_ff_1_qn, nand_1_out, nand_2_out, nand_3_out, nand_4_out, nand_5_out,
       nand_6_out, nand_7_out;

  Clock clock_1 (.out(clock_1_out));
  J_K_Flip_Flop j_k_ff_1 (.J(j), .K(k), .clk(clock_1_out), .Q(j_k_ff_1_q), .Qn(j_k_ff_1_qn));  // open: preset, reset
  nand nand_1 (nand_1_out, j, Q_prime, clock_1_out);
  nand nand_2 (nand_2_out, k, Q, clock_1_out);
  nand nand_3 (nand_3_out, clock_1_out, clock_1_out);
  nand nand_4 (nand_4_out, nand_1_out, nand_5_out);
  nand nand_5 (nand_5_out, nand_4_out, nand_2_out);
  J_K_Flip_Flop j_k_ff_2 (
    .J(j_k_ff_1_q), .K(j_k_ff_1_qn), .clk(nand_3_out), .Q(Q_2), .Qn(Q_prime_2));  // open: preset, reset
  nand nand_6 (nand_6_out, nand_4_out, nand_3_out);
  nand nand_7 (nand_7_out, nand_3_out, nand_5_out);
  nand nand_8 (Q, nand_6_out, Q_prime);
  nand nand_9 (Q_prime, Q, nand_7_out);

  // Notes on the sheet:
  //   clk
  //   JK master-slave Flip-flop
endmodule
