// Logisim project fileMultiplexer.circ as structural Verilog: 2 circuits, main circuit main
module main (
  input  I,
  input  s1,
  input  s2,
  output y0,
  output y1,
  output y2,
  output y3
);

  wire nand_1_out, nand_2_out, nand_3_out, nand_4_out, nand_5_out, nand_6_out, nand_7_out, nand_8_out,
       nand_9_out, nand_10_out, nand_11_out, nand_12_out, nand_13_out, nand_14_out;

  nand nand_1 (nand_1_out, 1'b1, s1);
  nand nand_2 (nand_2_out, 1'b1, s2);
  nand nand_3 (nand_3_out, I, nand_1_out);
  nand nand_4 (nand_4_out, I, nand_1_out);
  nand nand_5 (nand_5_out, I, s1);
  nand nand_6 (nand_6_out, I, s1);
  nand nand_7 (nand_7_out, nand_3_out, nand_3_out);
  nand nand_8 (nand_8_out, nand_4_out, nand_4_out);
  nand nand_9 (nand_9_out, nand_5_out, nand_5_out);
  nand nand_10 (nand_10_out, nand_6_out, nand_6_out);
  nand nand_11 (nand_11_out, nand_7_out, nand_2_out);
  nand nand_12 (nand_12_out, nand_8_out, s2);
  nand nand_13 (nand_13_out, nand_9_out, nand_2_out);
  nand nand_14 (nand_14_out, nand_10_out, s2);
  nand nand_15 (y0, nand_11_out, nand_11_out);
  nand nand_16 (y1, nand_12_out, nand_12_out);
  nand nand_17 (y2, nand_13_out, nand_13_out);
  nand nand_18 (y3, nand_14_out, nand_14_out);
endmodule

module MUX (
  input  I,
  input  s1,
  input  s2,
  output y0,
  output y1,
  output y2,
  output y3
);

  wire nand_1_out, nand_2_out, nand_3_out, nand_4_out, nand_5_out, nand_6_out, nand_7_out, nand_8_out,
       nand_9_out, nand_10_out, nand_11_out, nand_12_out, nand_13_out, nand_14_out;

  nand nand_1 (nand_1_out, 1'b1, s1);
  nand nand_2 (nand_2_out, 1'b1, s2);
  nand nand_3 (nand_3_out, I, nand_1_out);
  nand nand_4 (nand_4_out, I, nand_1_out);
  nand nand_5 (nand_5_out, I, s1);
  nand nand_6 (nand_6_out, I, s1);
  nand nand_7 (nand_7_out, nand_3_out, nand_3_out);
  nand nand_8 (nand_8_out, nand_4_out, nand_4_out);
  nand nand_9 (nand_9_out, nand_5_out, nand_5_out);
  nand nand_10 (nand_10_out, nand_6_out, nand_6_out);
  nand nand_11 (nand_11_out, nand_7_out, nand_2_out);
  nand nand_12 (nand_12_out, nand_8_out, s2);
  nand nand_13 (nand_13_out, nand_9_out, nand_2_out);
  nand nand_14 (nand_14_out, nand_10_out, s2);
  nand nand_15 (y0, nand_11_out, nand_11_out);
  nand nand_16 (y1, nand_12_out, nand_12_out);
  nand nand_17 (y2, nand_13_out, nand_13_out);
  nand nand_18 (y3, nand_14_out, nand_14_out);
endmodule
