// Logisim project fileSevenSeg.circ as structural Verilog: 1 circuit, main circuit main
module main (
  input  [3:0] i,
  output a,
  output b,
  output c,
  output d,
  output e,
  output f,
  output g
);

  wire nand_1_out, nand_2_out, nand_3_out, nand_4_out, nand_5_out, nand_6_out, nand_7_out, nand_8_out,
       nand_9_out, nand_10_out, nand_11_out, nand_12_out, nand_13_out, nand_14_out, nand_15_out, nand_16_out,
       nand_17_out, nand_18_out, nand_19_out, nand_20_out, nand_21_out, nand_22_out, nand_23_out,
       nand_24_out, nand_25_out, nand_26_out, nand_27_out, nand_29_out, nand_30_out, nand_31_out,
       nand_32_out, nand_33_out, nand_34_out, nand_35_out, nand_36_out, nand_38_out, nand_39_out,
       nand_40_out, nand_41_out, nand_42_out, nand_43_out, nand_44_out, nand_47_out, nand_48_out,
       nand_51_out, nand_52_out;

  nand nand_1 (nand_1_out, 1'b1, i[3]);
  nand nand_2 (nand_2_out, 1'b1, i[2]);
  nand nand_3 (nand_3_out, 1'b1, i[1]);
  nand nand_4 (nand_4_out, 1'b1, i[0]);
  nand nand_5 (nand_5_out, nand_2_out, nand_4_out);
  nand nand_6 (nand_6_out, i[2], i[0]);
  nand nand_7 (nand_7_out, i[1], i[0]);
  nand nand_8 (nand_8_out, i[3], nand_3_out);
  nand nand_9 (nand_9_out, i[1], nand_4_out);
  nand nand_10 (nand_10_out, nand_2_out, nand_4_out);
  nand nand_11 (nand_11_out, nand_2_out, i[1]);
  nand nand_12 (nand_12_out, i[2], nand_3_out);
  nand nand_13 (nand_13_out, nand_2_out, nand_4_out);
  nand nand_14 (nand_14_out, i[1], nand_4_out);
  nand nand_15 (nand_15_out, nand_3_out, nand_4_out);
  nand nand_16 (nand_16_out, i[2], nand_3_out);
  nand nand_17 (nand_17_out, i[2], nand_4_out);
  nand nand_18 (nand_18_out, nand_2_out, i[1]);
  nand nand_19 (nand_19_out, i[2], nand_3_out);
  nand nand_20 (nand_20_out, i[1], nand_4_out);
  nand nand_21 (nand_21_out, nand_5_out, nand_3_out);
  nand nand_22 (nand_22_out, nand_6_out, nand_1_out);
  nand nand_23 (nand_23_out, i[2], nand_7_out);
  nand nand_24 (nand_24_out, nand_8_out, nand_8_out);
  nand nand_25 (nand_25_out, nand_9_out, nand_9_out);
  nand nand_26 (nand_26_out, nand_10_out, nand_11_out);
  nand nand_27 (nand_27_out, nand_12_out, nand_12_out);
  nand nand_28 (c, nand_13_out, nand_14_out);
  nand nand_29 (nand_29_out, nand_15_out, nand_16_out);
  nand nand_30 (nand_30_out, nand_17_out, nand_1_out);
  nand nand_31 (nand_31_out, nand_18_out, nand_19_out);
  nand nand_32 (nand_32_out, nand_1_out, nand_20_out);
  nand nand_33 (nand_33_out, nand_21_out, nand_21_out);
  nand nand_34 (nand_34_out, nand_22_out, nand_22_out);
  nand nand_35 (nand_35_out, nand_23_out, nand_23_out);
  nand nand_36 (nand_36_out, nand_24_out, nand_4_out);
  nand nand_37 (c, nand_25_out, nand_2_out);
  nand nand_38 (nand_38_out, nand_26_out, nand_26_out);
  nand nand_39 (nand_39_out, nand_27_out, i[0]);
  nand nand_40 (nand_40_out, i[1], nand_4_out);
  nand nand_41 (nand_41_out, nand_29_out, nand_29_out);
  nand nand_42 (nand_42_out, nand_30_out, nand_30_out);
  nand nand_43 (nand_43_out, nand_31_out, nand_31_out);
  nand nand_44 (nand_44_out, nand_32_out, nand_32_out);
  nand nand_45 (a, nand_33_out, nand_34_out);
  nand nand_46 (b, nand_35_out, nand_36_out);
  nand nand_47 (nand_47_out, nand_38_out, nand_39_out);
  nand nand_48 (nand_48_out, nand_40_out, nand_1_out);
  nand nand_49 (f, nand_41_out, nand_42_out);
  nand nand_50 (f, nand_43_out, nand_44_out);
  nand nand_51 (nand_51_out, nand_47_out, nand_47_out);
  nand nand_52 (nand_52_out, nand_48_out, nand_48_out);
  nand nand_53 (c, nand_51_out, nand_52_out);
  _7_Segment_Display u_7_segment_display_1 (.g(f), .f(f), .a(a), .b(b), .e(c), .d(c), .c(c));  // open: dp

  assign d = c;
  assign e = c;
  assign g = f;
endmodule
