// Logisim project fulladder.circ as structural Verilog: 1 circuit, main circuit main
module main (
  input  [3:0] in_1,
  input  [1:0] in_2,
  input  [3:0] in_3,
  output [3:0] out_4,
  output C
);

  wire clock_1_out, d_ff_1_q;
  wire [3:0] shifter_1_out, shifter_2_out;

  Shifter #(.shift("lr"), .width(4)) shifter_1 (.in(in_1), .\dist (in_2), .out(shifter_1_out));
  Shifter #(.shift("lr"), .width(4)) shifter_2 (.in(in_3), .\dist (in_2), .out(shifter_2_out));
  Clock clock_1 (.out(clock_1_out));
  Adder #(.width(4)) adder_1 (.a(shifter_1_out), .b(shifter_2_out), .out(out_4), .cin(d_ff_1_q), .cout(C));
  D_Flip_Flop d_ff_1 (.D(C), .clk(clock_1_out), .Q(d_ff_1_q));  // open: Qn, preset, reset

  // Notes on the sheet:
  //   Sum
endmodule
